// Digital circuit MIPS.dig as structural Verilog
module MIPS (
  input  CLK
);

  wire add_2_s, and_1_out, multiplexer_1_out, multiplexer_3_out, multiplexer_5_out, ramdualport_1_d,
       Registradores_p1, Registradores_p6, shift_left_2_out, ula_1_p4;
  wire [1:0] PC_q, ula_1_p3;
  wire [15:0] add_s, multiplexer_2_out;
  wire [15:1] undriven;
  wire [31:0] bitextender_1_out, \Memória_de_Instrução_d , multiplexer_4_out, Registradores_p7;

  Add add (.a(PC_q[0]), .b(1'b0), .c_i(1'b0), .s(add_s[0]));  // open: c_o
  Multiplexer multiplexer_1 (.in_0(multiplexer_2_out[0]), .out(multiplexer_1_out));  // open: sel, in_1
  Multiplexer #(.Bits(16), .Selector_Bits(2)) multiplexer_2 (
    .in_0(add_s), .in_3({undriven, 1'b0}), .out(multiplexer_2_out));  // open: sel, in_1, in_2
  Register PC (.D(multiplexer_1_out), .C(CLK), .Q(PC_q[0]));  // open: en
  ROM \Memória_de_Instrução  (.A(PC_q), .sel(1'b1), .D(\Memória_de_Instrução_d [0]));
  BarrelShifter shift_left (.in(\Memória_de_Instrução_d [0]), .shift(6'b000010), .out(add_s[0]));
  ROM #(.Bits(6)) Unidade_de_Controle (.A(\Memória_de_Instrução_d [27:26]), .sel(1'b1));  // open: D
  Multiplexer multiplexer_3 (
    .in_0(\Memória_de_Instrução_d [16]), .in_1(\Memória_de_Instrução_d [11]), .out(multiplexer_3_out));  // open: sel
  BitExtender #(.inputBits(16), .outputBits(32)) bitextender_1 (
    .in(\Memória_de_Instrução_d [15:0]), .out(bitextender_1_out));
  // registradores Registradores: pin names not known; wires that end beside it: Registradores_p1, CLK, multiplexer_3_out, \Memória_de_Instrução_d [25:21], \Memória_de_Instrução_d [20:16], Registradores_p6, Registradores_p7
  BarrelShifter shift_left_2 (.in(bitextender_1_out[0]), .shift(6'b000010), .out(shift_left_2_out));
  Multiplexer #(.Bits(32)) multiplexer_4 (
    .in_0(Registradores_p7), .in_1(bitextender_1_out), .out(multiplexer_4_out));  // open: sel
  Add add_2 (.a(add_s[0]), .b(shift_left_2_out), .s(add_2_s));  // open: c_i, c_o
  buf and_1 (and_1_out, ula_1_p4);  // And open: In_1
  // ULA ula_1: pin names not known; wires that end beside it: Registradores_p6, multiplexer_4_out, ula_1_p3, ula_1_p4
  Multiplexer multiplexer_5 (.sel(and_1_out), .in_0(add_s[0]), .in_1(add_2_s), .out(multiplexer_5_out));
  Multiplexer multiplexer_6 (.in_0(multiplexer_5_out), .in_1(add_s[0]), .out(multiplexer_1_out));  // open: sel
  RAMDualPort ramdualport_1 (.A(ula_1_p3), .Din(Registradores_p7[0]), .C(CLK), .D(ramdualport_1_d));  // open: str, ld
  Multiplexer multiplexer_7 (.in_0(multiplexer_4_out[0]), .in_1(ramdualport_1_d), .out(Registradores_p1));  // open: sel
  // Pins of 1 and 32 bits meet at Registradores_p7
  // Pins of 1 and 32 bits meet at bitextender_1_out
  // Pins of 1 and 32 bits meet at multiplexer_4_out
  // Pins of 1 and 5 bits meet at \Memória_de_Instrução_d [20:16]
  // Pins of 1 and 5 bits meet at \Memória_de_Instrução_d [15:11]
  // Pins of 1 and 32 bits meet at \Memória_de_Instrução_d 
  // Pins of 1 and 26 bits meet at \Memória_de_Instrução_d [25:0]
  // Pins of 2 and 6 bits meet at \Memória_de_Instrução_d [31:26]
  // Pins of 1 and 2 bits meet at PC_q
  // Pins of 1 and 4 bits meet at 4'b0100
  // Pins of 1 and 16 bits meet at add_s
  // Pins of 1 and 16 bits meet at {undriven, 1'b0}
endmodule
